# Fritzing sketch aquarium1 (saved by Fritzing 1.0.8)
breadboards: 1

parts:
  M1 = DOIT Esp32 DevKit v1 (30 pins long, 11 pins width) [part_number=ESP32S-PIN30]
  KF-1 = KF-301 Relay [package=THT]  # not connected
  KF-2 = KF-301 Relay [package=THT]
  KF-3 = KF-301 Relay [package=THT]
  KF-4 = KF-301 Relay [package=THT]
  KF-5 = KF-301 Relay [package=THT]

nets:
  N1: M1.3V3, KF-2.power, KF-3.power, KF-4.power, KF-5.power
  N2: M1.GND, KF-2.ground, KF-3.ground, KF-4.ground, KF-5.ground
  N3: M1.D4, KF-5.signal
  N4: M1.D18, KF-4.signal
  N5: M1.D19, KF-3.signal
  N6: M1.D21, KF-2.signal

notes:
  GND / 3V HUB
  LAPTOP
  MONITOR
  AERATOR
  LAMPU AQUA

custom parts:
  DOIT Esp32 DevKit v1 (30 pins long, 11 pins width): The DOIT Esp32 DevKit v1 is one of the development board created by DOIT to evaluate the ESP-WROOM-32 module. It is based on the ESP32 microcontroller that boasts Wifi, Bluetooth, Ethernet and Low Power support all in a single chip. (vanepp) made breadboard work, adjusted pin numbering and labels and reduced size of schematic and cleaned up pcb. This chip is 30pins long (2 x15) and 11 pins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
  KF-301 Relay: KF-301
