# Fritzing sketch carlos-esp32 (saved by Fritzing 1.0.6)
breadboards: 1

parts:
  M1 = DOIT Esp32 DevKit v1 (30 pins long, 11 pins width) [part_number=ESP32S-PIN30]
  KF-1 = KF-301 Relay [package=THT]

nets:
  N1: M1.3V3, KF-1.power
  N2: M1.GND, KF-1.ground
  N3: M1.D22, KF-1.signal

custom parts:
  DOIT Esp32 DevKit v1 (30 pins long, 11 pins width): The DOIT Esp32 DevKit v1 is one of the development board created by DOIT to evaluate the ESP-WROOM-32 module. It is based on the ESP32 microcontroller that boasts Wifi, Bluetooth, Ethernet and Low Power support all in a single chip. (vanepp) made breadboard work, adjusted pin numbering and labels and reduced size of schematic and cleaned up pcb. This chip is 30pins long (2 x15) and 11 pins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
  KF-301 Relay: KF-301
